// Logisim project CIRCUITO.circ as structural Verilog: 1 circuit, main circuit main
module main (
  input  A,
  input  B,
  input  in_3,
  output out_4,
  output out_5
);

  wire and_1_out, and_2_out, or_1_out, xor_1_out;

  xor xor_1 (xor_1_out, A, B);
  or or_1 (or_1_out, B, in_3);
  xor xor_2 (out_4, xor_1_out, in_3);
  and and_1 (and_1_out, or_1_out, A);
  and and_2 (and_2_out, B, in_3);
  or or_2 (out_5, and_1_out, and_2_out);
endmodule
