// Logisim project ADD4.circ as structural Verilog
module main (
  input  [3:0] in_1,
  input  [3:0] in_2,
  input  in_3,
  input  in_4,
  input  in_5,
  output [3:0] out_6,
  output out_7,
  output out_8,
  output out_9
);

  add_1 add_1_1 (.A(in_4), .B(in_3), .in_3(in_5), .out_4(out_9), .out_5(out_8));
  add_4 add_4_1 (.in_2(in_2), .in_1(in_1), .out_4(out_6), .out_3(out_7));
endmodule

module add_1 (
  input  A,
  input  B,
  input  in_3,
  output out_4,
  output out_5
);

  wire and_1_out, and_2_out, or_1_out, xor_1_out;

  xor xor_1 (xor_1_out, A, B);
  or or_1 (or_1_out, B, in_3);
  xor xor_2 (out_4, xor_1_out, in_3);
  and and_1 (and_1_out, or_1_out, A);
  and and_2 (and_2_out, B, in_3);
  or or_2 (out_5, and_1_out, and_2_out);
endmodule

module add_2 (
  input  in_1,
  input  in_2,
  input  in_3,
  output out_4,
  output out_5
);

  add_1 add_1_1 (.A(in_2), .B(in_1), .in_3(in_3), .out_4(out_5), .out_5(out_4));
endmodule

module add_4 (
  input  [3:0] in_1,
  input  [3:0] in_2,
  output out_3,
  output [3:0] out_4
);

  wire add_1_2_out_5, add_1_3_out_5, add_1_4_out_5;

  add_1 add_1_1 (.A(in_1[3]), .B(in_2[3]), .in_3(add_1_2_out_5), .out_4(out_4[3]), .out_5(out_3));
  add_1 add_1_2 (.A(in_1[2]), .B(in_2[2]), .in_3(add_1_3_out_5), .out_4(out_4[2]), .out_5(add_1_2_out_5));
  add_1 add_1_3 (.A(in_1[1]), .B(in_2[1]), .in_3(add_1_4_out_5), .out_4(out_4[1]), .out_5(add_1_3_out_5));
  add_1 add_1_4 (.A(in_1[0]), .B(in_2[0]), .in_3(1'b0), .out_4(out_4[0]), .out_5(add_1_4_out_5));
endmodule
